// Logisim project Lab_Week1.circ as structural Verilog: 1 circuit, main circuit main
module main (
  input  Pin_1,
  input  Input_1,
  input  Pin_2,
  input  Input_2,
  input  Pin_1_2,
  input  Pin_2_2,
  input  in_7,
  input  Pin_1_3,
  input  Pin_2_3,
  input  Carry_In
);

  wire and_1_out, and_2_out, and_3_out, and_4_out, nand_1_out, not_1_out, or_1_out, xor_1_out, xor_2_out,
       xor_3_out;

  and and_1 (and_1_out, Pin_1, Pin_2);
  nand nand_1 (nand_1_out, Pin_1_2, Pin_2_2);
  xor xor_1 (xor_1_out, Pin_1_3, Pin_2_3);
  LED led_1 (.in(and_1_out));
  LED led_2 (.in(nand_1_out));
  and and_2 (and_2_out, Pin_1_3, Pin_2_3);
  and and_3 (and_3_out, xor_1_out, Carry_In);
  xor xor_2 (xor_2_out, xor_1_out, Carry_In);
  or or_1 (or_1_out, and_2_out, and_3_out);
  LED led_3 (.in(xor_2_out));
  LED led_4 (.in(or_1_out));
  and and_4 (and_4_out, Input_1, Input_2);
  not not_1 (not_1_out, in_7);
  xor xor_3 (xor_3_out, Input_1, Input_2);
  LED led_5 (.in(xor_3_out));
  LED led_6 (.in(and_4_out));
  LED led_7 (.in(not_1_out));

  // Notes on the sheet:
  //   Sum
  //   Carry Output
  //   Sum
  //   Carry
endmodule
