// Logisim project Lab_Week2_1.circ as structural Verilog: 1 circuit, main circuit main
module main (
  input  Input_1,
  input  Input_2,
  input  Pin_1,
  input  Pin_2,
  input  Pin_1_2,
  input  Pin_2_2,
  input  Pin_1_3,
  input  Pin_2_3
);

  wire and_1_out, and_2_out, and_3_out, and_4_out, and_5_out, and_6_out, and_7_out, or_1_out, or_2_out,
       or_3_out, xor_1_out, xor_2_out, xor_3_out, xor_4_out, xor_5_out, xor_6_out, xor_7_out;

  xor xor_1 (xor_1_out, Input_1, Input_2);
  and and_1 (and_1_out, Input_1, Input_2);
  xor xor_2 (xor_2_out, Pin_1, Pin_2);
  xor xor_3 (xor_3_out, Pin_1_2, Pin_2_2);
  xor xor_4 (xor_4_out, Pin_1_3, Pin_2_3);
  LED led_1 (.in(and_1_out));
  and and_2 (and_2_out, Pin_1, Pin_2);
  and and_3 (and_3_out, xor_2_out, and_1_out);
  and and_4 (and_4_out, Pin_1_2, Pin_2_2);
  and and_5 (and_5_out, xor_3_out, or_1_out);
  and and_6 (and_6_out, Pin_1_3, Pin_2_3);
  and and_7 (and_7_out, xor_4_out, or_2_out);
  xor xor_5 (xor_5_out, xor_2_out, and_1_out);
  or or_1 (or_1_out, and_2_out, and_3_out);
  xor xor_6 (xor_6_out, xor_3_out, or_1_out);
  or or_2 (or_2_out, and_4_out, and_5_out);
  xor xor_7 (xor_7_out, xor_4_out, or_2_out);
  or or_3 (or_3_out, and_6_out, and_7_out);
  LED led_2 (.in(or_1_out));
  LED led_3 (.in(or_2_out));
  LED led_4 (.in(or_3_out));
  LED led_5 (.in(xor_1_out));
  LED led_6 (.in(xor_5_out));
  LED led_7 (.in(xor_6_out));
  LED led_8 (.in(xor_7_out));

  // Notes on the sheet:
  //   Carry In
  //   Carry In
  //   Carry In
  //   Carry
  //   Carry Output
  //   Carry Output
  //   Carry Output
  //   Sum
  //   Sum
  //   Sum
  //   Sum
endmodule
