// Logisim project Lab_Week2_2.circ as structural Verilog: 1 circuit, main circuit main
module main (
  input  Set,
  input  Reset,
  input  D,
  output Q_prime,
  output Q,
  output Q_2,
  output Q_prime_2
);

  wire and_1_out, and_2_out, clock_1_out, not_1_out;

  Clock clock_1 (.out(clock_1_out));
  not not_1 (not_1_out, D);
  and and_1 (and_1_out, not_1_out, clock_1_out);
  and and_2 (and_2_out, D, clock_1_out);
  nor nor_1 (Q_prime, Set, Q);
  nor nor_2 (Q, Q_prime, Reset);
  nor nor_3 (Q_2, and_1_out, Q_prime_2);
  nor nor_4 (Q_prime_2, Q_2, and_2_out);

  // Notes on the sheet:
  //   Clock
endmodule
